// Logisim project MM4001.circ as structural Verilog: 3 circuits, main circuit main
module main (
  input  [7:0] in_1
);

  wire clock_1_out;
  wire [3:0] alu_1_out_4, register_1_a, register_1_d;

  Clock clock_1 (.out(clock_1_out));
  ALU alu_1 (.in_1(in_1), .A(register_1_a), .D(register_1_d), .out_4(alu_1_out_4));  // open: out_5, out_6, out_7
  Register register_1 (
    .Befehlsbus(in_1), .ALU(alu_1_out_4), .A(register_1_a), .D(register_1_d), .in_3(clock_1_out));  // open: Addresse
endmodule

module Register (
  input  [7:0] Befehlsbus,
  input  [3:0] ALU,
  input  in_3,
  output [3:0] A,
  output [3:0] D,
  output [7:0] Addresse
);

  wire and_1_out, comparator_1_eq, comparator_2_eq, comparator_3_eq, comparator_4_gt, comparator_4_lt,
       decoder_1_out0, decoder_1_out1, decoder_1_out2, decoder_1_out3, or_1_out, or_2_out;
  wire [3:0] controlled_buffer_1_out, multiplexer_1_out, or_3_out;

  Comparator #(.width(4), .mode("unsigned")) comparator_1 (
    .a(Befehlsbus[7:4]), .b(4'b0001), .eq(comparator_1_eq));  // open: gt, lt
  Comparator #(.width(4), .mode("unsigned")) comparator_2 (
    .a(Befehlsbus[7:4]), .b(4'b0010), .eq(comparator_2_eq));  // open: gt, lt
  Comparator #(.width(4), .mode("unsigned")) comparator_3 (
    .a(Befehlsbus[7:4]), .b(4'b0101), .eq(comparator_3_eq));  // open: gt, lt
  Comparator #(.width(4), .mode("unsigned")) comparator_4 (
    .a(Befehlsbus[3:0]), .b(4'b0100), .gt(comparator_4_gt), .lt(comparator_4_lt));  // open: eq
  Decoder #(.select(2), .disabled(0)) decoder_1 (
    .out0(decoder_1_out0), .out1(decoder_1_out1), .out2(decoder_1_out2), .out3(decoder_1_out3),
    .sel(Befehlsbus[3:2]), .en(comparator_1_eq));
  and and_1 (and_1_out, comparator_3_eq, or_1_out);
  or or_1 (or_1_out, comparator_4_gt, comparator_4_lt);
  assign controlled_buffer_1_out = comparator_2_eq ? Befehlsbus[3:0] : 4'bz;  // Controlled_Buffer controlled_buffer_1
  Pull_Resistor pull_resistor_1 (.node(controlled_buffer_1_out));
  Pull_Resistor pull_resistor_2 (.node(ALU));
  or or_2 (or_2_out, decoder_1_out0, and_1_out, comparator_2_eq);
  assign or_3_out = controlled_buffer_1_out | ALU | multiplexer_1_out;  // OR_Gate or_3, 4 bits wide
  Register_part #(.width(4)) u_A (.D(or_3_out), .en(or_2_out), .Q(A), .clk(in_3));  // open: clr
  Register_part #(.width(4)) u_D (.D(or_3_out), .en(decoder_1_out1), .Q(D), .clk(in_3));  // open: clr
  Register_part #(.width(4)) PL (.D(or_3_out), .en(decoder_1_out2), .Q(Addresse[3:0]), .clk(in_3));  // open: clr
  Register_part #(.width(4)) PH (.D(or_3_out), .en(decoder_1_out3), .Q(Addresse[7:4]), .clk(in_3));  // open: clr
  Multiplexer #(.select(2), .width(4), .disabled(0)) multiplexer_1 (
    .in0(A), .in1(D), .in2(Addresse[3:0]), .in3(Addresse[7:4]), .out(multiplexer_1_out),
    .sel(Befehlsbus[1:0]), .en(comparator_1_eq));

  // Notes on the sheet:
  //   MOV
  //   INA
endmodule

module ALU (
  input  [7:0] in_1,
  input  [3:0] A,
  input  [3:0] D,
  output [3:0] out_4,
  output out_5,
  output out_6,
  output out_7
);

  wire comparator_1_eq;
  wire [3:0] adder_1_out, adder_2_out, and_1_out, controlled_buffer_1_out, controlled_buffer_2_out,
       nand_1_out, nor_1_out, not_1_out, or_1_out, shifter_1_out, shifter_2_out, shifter_3_out,
       shifter_4_out, subtractor_1_out, subtractor_2_out, xnor_1_out, xor_1_out;

  Comparator #(.width(4), .mode("unsigned")) comparator_1 (
    .a(in_1[7:4]), .b(4'b0101), .eq(comparator_1_eq));  // open: gt, lt
  assign controlled_buffer_1_out = comparator_1_eq ? A : 4'bz;  // Controlled_Buffer controlled_buffer_1
  Pull_Resistor pull_resistor_1 (.node(controlled_buffer_1_out));
  assign controlled_buffer_2_out = comparator_1_eq ? D : 4'bz;  // Controlled_Buffer controlled_buffer_2
  Pull_Resistor pull_resistor_2 (.node(controlled_buffer_2_out));
  Adder #(.width(4)) adder_1 (
    .a(controlled_buffer_1_out), .b(controlled_buffer_2_out), .out(adder_1_out));  // open: cin, cout
  Subtractor #(.width(4)) subtractor_1 (
    .a(controlled_buffer_1_out), .b(controlled_buffer_2_out), .out(subtractor_1_out));  // open: bin, bout
  Adder #(.width(4)) adder_2 (.a(controlled_buffer_1_out), .b(4'b0001), .out(adder_2_out));  // open: cin, cout
  Subtractor #(.width(4)) subtractor_2 (
    .a(controlled_buffer_1_out), .b(4'b0001), .out(subtractor_2_out));  // open: bin, bout
  Comparator #(.width(4), .mode("unsigned")) comparator_2 (
    .a(controlled_buffer_1_out), .b(controlled_buffer_2_out), .gt(out_5), .eq(out_6), .lt(out_7));
  assign not_1_out = ~controlled_buffer_2_out;  // NOT_Gate not_1, 4 bits wide
  assign and_1_out = controlled_buffer_2_out & controlled_buffer_1_out;  // AND_Gate and_1, 4 bits wide
  assign nand_1_out = ~(controlled_buffer_2_out & controlled_buffer_1_out);  // NAND_Gate nand_1, 4 bits wide
  assign or_1_out = controlled_buffer_2_out | controlled_buffer_1_out;  // OR_Gate or_1, 4 bits wide
  assign nor_1_out = ~(controlled_buffer_2_out | controlled_buffer_1_out);  // NOR_Gate nor_1, 4 bits wide
  assign xor_1_out = controlled_buffer_2_out ^ controlled_buffer_1_out;  // XOR_Gate xor_1, 4 bits wide
  assign xnor_1_out = ~(controlled_buffer_2_out ^ controlled_buffer_1_out);  // XNOR_Gate xnor_1, 4 bits wide
  Shifter #(.width(4)) shifter_1 (
    .in(controlled_buffer_2_out), .\dist (controlled_buffer_1_out[1:0]), .out(shifter_1_out));
  Shifter #(.width(4), .shift("lr")) shifter_2 (
    .in(controlled_buffer_2_out), .\dist (controlled_buffer_1_out[1:0]), .out(shifter_2_out));
  Shifter #(.width(4), .shift("rl")) shifter_3 (
    .in(controlled_buffer_2_out), .\dist (controlled_buffer_1_out[1:0]), .out(shifter_3_out));
  Shifter #(.width(4), .shift("rr")) shifter_4 (
    .in(controlled_buffer_2_out), .\dist (controlled_buffer_1_out[1:0]), .out(shifter_4_out));
  Multiplexer #(.select(4), .width(4), .disabled(0)) multiplexer_1 (
    .in0(adder_1_out), .in1(subtractor_1_out), .in2(adder_2_out), .in3(subtractor_2_out), .in4(4'b0000),
    .in5(not_1_out), .in6(and_1_out), .in7(nand_1_out), .in8(or_1_out), .in9(nor_1_out), .in10(xor_1_out),
    .in11(xnor_1_out), .in12(shifter_1_out), .in13(shifter_2_out), .in14(shifter_3_out),
    .in15(shifter_4_out), .out(out_4), .sel(in_1[3:0]), .en(comparator_1_eq));
endmodule
