// Logisim project Microcontroler.circ as structural Verilog: 5 circuits, main circuit main
// X
module main (
  input  [7:0] in_1,
  input  [7:0] in_2,
  input  [7:0] in_3,
  input  [7:0] in_4,
  input  [7:0] in_5,
  input  [7:0] in_6,
  input  [7:0] in_7,
  input  [7:0] in_8,
  output [7:0] out_9,
  output [7:0] out_10,
  output [7:0] out_11,
  output [7:0] out_12,
  output [7:0] out_13,
  output [7:0] out_14,
  output [7:0] out_15,
  output [7:0] out_16
);

  wire clock_1_out, comparator_2_eq, decoder_1_out3, decoder_1_out4, decoder_1_out5, decoder_1_out6,
       decoder_1_out7, decoder_1_out8, decoder_1_out9, decoder_1_out10, decoder_1_out11, decoder_1_out12,
       decoder_1_out13, decoder_1_out14, decoder_1_out15, or_1_out, or_2_out, Reset_out;
  wire [2:0] comparator_1_gt, decoder_1_out2;
  wire [3:0] program_1_out_7;
  wire [7:0] adder_1_out, and_1_out, bit_extender_1_out, controlled_buffer_1_out, controlled_buffer_2_out,
       divider_1_out, mem_control_1_out_14, multiplier_1_out, not_1_out, or_3_out, program_1_out_8,
       random_1_out, shifter_1_out, subtractor_1_out, v_ctrl_1_out_5, v_ctrl_1_out_6, xor_1_out;
  wire [11:0] rom_1_data;
  wire [15:0] program_1_out_6;

  Clock clock_1 (.out(clock_1_out));
  Button Reset (.out(Reset_out));
  Program program_1 (
    .in_3(decoder_1_out10), .in_4(Reset_out), .in_5(clock_1_out), .in_2(controlled_buffer_1_out),
    .out_6(program_1_out_6), .in_1(rom_1_data), .out_7(program_1_out_7), .out_8(program_1_out_8));
  Decoder #(.select(4)) decoder_1 (
    .out0(decoder_1_out2[2]), .out1(decoder_1_out2[1]), .out2(decoder_1_out2[0]), .out3(decoder_1_out3),
    .out4(decoder_1_out4), .out5(decoder_1_out5), .out6(decoder_1_out6), .out7(decoder_1_out7),
    .out8(decoder_1_out8), .out9(decoder_1_out9), .out10(decoder_1_out10), .out11(decoder_1_out11),
    .out12(decoder_1_out12), .out13(decoder_1_out13), .out14(decoder_1_out14), .out15(decoder_1_out15),
    .sel(program_1_out_7));  // open: en
  Mem_Control mem_control_1 (
    .in_6(in_1), .in_7(in_2), .in_8(in_3), .in_9(in_4), .in_10(in_5), .in_11(in_6), .in_12(in_7),
    .in_13(in_8), .out_15(out_9), .out_16(out_10), .out_17(out_11), .out_18(out_12), .out_19(out_13),
    .out_20(out_14), .out_21(out_15), .out_22(out_16), .in_2(program_1_out_8), .in_3(or_1_out),
    .in_4(controlled_buffer_2_out), .out_14(mem_control_1_out_14), .in_5(Reset_out), .in_1(clock_1_out));
  ROM #(.addrWidth(16), .dataWidth(12)) rom_1 (.addr(program_1_out_6), .data(rom_1_data));  // open: sel
  or or_1 (or_1_out, decoder_1_out3, decoder_1_out4, decoder_1_out5, decoder_1_out6, decoder_1_out7, decoder_1_out8, decoder_1_out9, decoder_1_out11, decoder_1_out12, decoder_1_out13, decoder_1_out14, decoder_1_out15);
  V_Ctrl v_ctrl_1 (
    .in_1(mem_control_1_out_14), .in_2(program_1_out_8), .in_3(decoder_1_out2), .out_5(v_ctrl_1_out_5),
    .out_6(v_ctrl_1_out_6), .in_4(Reset_out));
  assign controlled_buffer_1_out = or_2_out ? v_ctrl_1_out_5 : 8'bz;  // Controlled_Buffer controlled_buffer_1
  or or_2 (or_2_out, decoder_1_out10, comparator_2_eq);
  Adder adder_1 (.a(v_ctrl_1_out_6), .b(v_ctrl_1_out_5), .out(adder_1_out));  // open: cin, cout
  Subtractor subtractor_1 (.a(v_ctrl_1_out_6), .b(v_ctrl_1_out_5), .out(subtractor_1_out));  // open: bin, bout
  Multiplier multiplier_1 (.a(v_ctrl_1_out_6), .b(v_ctrl_1_out_5), .out(multiplier_1_out));  // open: cin, cout
  Divider divider_1 (.a(v_ctrl_1_out_6), .b(v_ctrl_1_out_5), .out(divider_1_out));  // open: upper, rem
  Comparator comparator_1 (
    .a(v_ctrl_1_out_6), .b(v_ctrl_1_out_5), .gt(comparator_1_gt[0]), .eq(comparator_1_gt[1]),
    .lt(comparator_1_gt[2]));
  assign bit_extender_1_out = {{5{1'b0}}, comparator_1_gt};  // Bit_Extender bit_extender_1
  Shifter #(.shift("rl")) shifter_1 (.in(v_ctrl_1_out_6), .\dist (v_ctrl_1_out_5[2:0]), .out(shifter_1_out));
  Comparator comparator_2 (.a(program_1_out_8), .b(v_ctrl_1_out_6), .eq(comparator_2_eq));  // open: gt, lt
  Random random_1 (.clk(clock_1_out), .out(random_1_out));  // open: next, clr
  assign and_1_out = v_ctrl_1_out_6 & v_ctrl_1_out_5;  // AND_Gate and_1, 8 bits wide
  assign or_3_out = v_ctrl_1_out_6 | v_ctrl_1_out_5;  // OR_Gate or_3, 8 bits wide
  assign xor_1_out = v_ctrl_1_out_6 ^ v_ctrl_1_out_5;  // XOR_Gate xor_1, 8 bits wide
  assign not_1_out = ~v_ctrl_1_out_6;  // NOT_Gate not_1, 8 bits wide
  assign controlled_buffer_2_out = decoder_1_out13 ? or_3_out : 8'bz;  // Controlled_Buffer controlled_buffer_2
  assign controlled_buffer_2_out = decoder_1_out14 ? xor_1_out : 8'bz;  // Controlled_Buffer controlled_buffer_3
  assign controlled_buffer_2_out = decoder_1_out15 ? not_1_out : 8'bz;  // Controlled_Buffer controlled_buffer_4
  assign controlled_buffer_2_out = decoder_1_out9 ? shifter_1_out : 8'bz;  // Controlled_Buffer controlled_buffer_5
  assign controlled_buffer_2_out = decoder_1_out11 ? random_1_out : 8'bz;  // Controlled_Buffer controlled_buffer_6
  assign controlled_buffer_2_out = decoder_1_out12 ? and_1_out : 8'bz;  // Controlled_Buffer controlled_buffer_7
  assign controlled_buffer_2_out = decoder_1_out5 ? subtractor_1_out : 8'bz;  // Controlled_Buffer controlled_buffer_8
  assign controlled_buffer_2_out = decoder_1_out6 ? multiplier_1_out : 8'bz;  // Controlled_Buffer controlled_buffer_9
  assign controlled_buffer_2_out = decoder_1_out7 ? divider_1_out : 8'bz;  // Controlled_Buffer controlled_buffer_10
  assign controlled_buffer_2_out = decoder_1_out8 ? bit_extender_1_out : 8'bz;  // Controlled_Buffer controlled_buffer_11
  assign controlled_buffer_2_out = decoder_1_out3 ? v_ctrl_1_out_6 : 8'bz;  // Controlled_Buffer controlled_buffer_12
  assign controlled_buffer_2_out = decoder_1_out4 ? adder_1_out : 8'bz;  // Controlled_Buffer controlled_buffer_13

  // Notes on the sheet:
  //   vo - v1
  //   V0-      -V1
endmodule

module Program (
  input  [11:0] in_1,
  input  [7:0] in_2,
  input  in_3,
  input  in_4,
  input  in_5,
  output [15:0] out_6,
  output [3:0] out_7,
  output [7:0] out_8
);

  wire not_1_out, or_1_out, or_2_out;
  wire [15:0] adder_1_out, controlled_buffer_1_out;

  or or_1 (or_1_out, in_2[0], in_2[1], in_2[2], in_2[3], in_2[4], in_2[5], in_2[6], in_2[7]);
  assign controlled_buffer_1_out = or_1_out ? {in_2, 8'h1} : 16'bz;  // Controlled_Buffer controlled_buffer_1
  Pull_Resistor pull_resistor_1 (.node(in_2));
  not not_1 (not_1_out, or_1_out);
  assign controlled_buffer_1_out = not_1_out ? adder_1_out : 16'bz;  // Controlled_Buffer controlled_buffer_2
  Register #(.width(16)) register_1 (.D(controlled_buffer_1_out), .Q(out_6), .clk(or_2_out), .clr(in_4));  // open: en
  or or_2 (or_2_out, in_3, in_5);
  Adder #(.width(16)) adder_1 (.a(out_6), .b(16'h1), .out(adder_1_out));  // open: cin, cout

  assign out_7 = in_1[11:8];
  assign out_8 = in_1[7:0];
endmodule

module Mem_Control (
  input  in_1,
  input  [7:0] in_2,
  input  in_3,
  input  [7:0] in_4,
  input  in_5,
  input  [7:0] in_6,
  input  [7:0] in_7,
  input  [7:0] in_8,
  input  [7:0] in_9,
  input  [7:0] in_10,
  input  [7:0] in_11,
  input  [7:0] in_12,
  input  [7:0] in_13,
  output [7:0] out_14,
  output [7:0] out_15,
  output [7:0] out_16,
  output [7:0] out_17,
  output [7:0] out_18,
  output [7:0] out_19,
  output [7:0] out_20,
  output [7:0] out_21,
  output [7:0] out_22
);

  wire and_1_out, and_2_out, and_3_out, and_4_out, and_5_out, and_6_out, and_7_out, and_8_out, and_9_out,
       decoder_1_out0, decoder_1_out1, decoder_1_out2, decoder_1_out3, decoder_1_out4, decoder_1_out5,
       decoder_1_out6, decoder_1_out7, decoder_2_out0, decoder_2_out1, decoder_2_out2, decoder_2_out3,
       decoder_2_out4, decoder_2_out5, decoder_2_out6, decoder_2_out7, decoder_2_out8, decoder_2_out9,
       decoder_2_out10, decoder_2_out11, decoder_2_out12, decoder_2_out13, decoder_2_out14, decoder_2_out15;
  wire [7:0] OutPuts;

  assign in_4 = decoder_1_out0 ? in_6 : 8'bz;  // Controlled_Buffer controlled_buffer_1
  assign in_4 = decoder_1_out1 ? in_7 : 8'bz;  // Controlled_Buffer controlled_buffer_2
  assign in_4 = decoder_1_out2 ? in_8 : 8'bz;  // Controlled_Buffer controlled_buffer_3
  assign in_4 = decoder_1_out3 ? in_9 : 8'bz;  // Controlled_Buffer controlled_buffer_4
  assign in_4 = decoder_1_out4 ? in_10 : 8'bz;  // Controlled_Buffer controlled_buffer_5
  assign in_4 = decoder_1_out5 ? in_11 : 8'bz;  // Controlled_Buffer controlled_buffer_6
  assign in_4 = decoder_1_out6 ? in_12 : 8'bz;  // Controlled_Buffer controlled_buffer_7
  Decoder #(.select(4), .disabled(0)) decoder_1 (
    .out0(decoder_1_out0), .out1(decoder_1_out1), .out2(decoder_1_out2), .out3(decoder_1_out3),
    .out4(decoder_1_out4), .out5(decoder_1_out5), .out6(decoder_1_out6), .out7(decoder_1_out7),
    .out8(OutPuts[7]), .out9(OutPuts[6]), .out10(OutPuts[5]), .out11(OutPuts[4]), .out12(OutPuts[3]),
    .out13(OutPuts[2]), .out14(OutPuts[1]), .out15(OutPuts[0]), .sel(in_2[3:0]), .en(decoder_2_out0));
  assign in_4 = decoder_1_out7 ? in_13 : 8'bz;  // Controlled_Buffer controlled_buffer_8
  _4_bit_Mem u_4_bit_mem_1 (
    .in_4(out_14), .out_6(in_4), .in_1(in_2[3:0]), .in_2(and_1_out), .in_3(decoder_2_out1), .in_5(in_5));
  _4_bit_Mem u_4_bit_mem_2 (
    .in_4(out_14), .out_6(in_4), .in_1(in_2[3:0]), .in_2(and_1_out), .in_3(decoder_2_out2), .in_5(in_5));
  Decoder #(.select(4)) decoder_2 (
    .out0(decoder_2_out0), .out1(decoder_2_out1), .out2(decoder_2_out2), .out3(decoder_2_out3),
    .out4(decoder_2_out4), .out5(decoder_2_out5), .out6(decoder_2_out6), .out7(decoder_2_out7),
    .out8(decoder_2_out8), .out9(decoder_2_out9), .out10(decoder_2_out10), .out11(decoder_2_out11),
    .out12(decoder_2_out12), .out13(decoder_2_out13), .out14(decoder_2_out14), .out15(decoder_2_out15),
    .sel(in_2[7:4]));  // open: en
  _4_bit_Mem u_4_bit_mem_3 (
    .in_4(out_14), .out_6(in_4), .in_1(in_2[3:0]), .in_2(and_1_out), .in_3(decoder_2_out3), .in_5(in_5));
  _4_bit_Mem u_4_bit_mem_4 (
    .in_4(out_14), .out_6(in_4), .in_1(in_2[3:0]), .in_2(and_1_out), .in_3(decoder_2_out4), .in_5(in_5));
  _4_bit_Mem u_4_bit_mem_5 (
    .in_4(out_14), .out_6(in_4), .in_1(in_2[3:0]), .in_2(and_1_out), .in_3(decoder_2_out5), .in_5(in_5));
  _4_bit_Mem u_4_bit_mem_6 (
    .in_4(out_14), .out_6(in_4), .in_1(in_2[3:0]), .in_2(and_1_out), .in_3(decoder_2_out6), .in_5(in_5));
  _4_bit_Mem u_4_bit_mem_7 (
    .in_4(out_14), .out_6(in_4), .in_1(in_2[3:0]), .in_2(and_1_out), .in_3(decoder_2_out7), .in_5(in_5));
  _4_bit_Mem u_4_bit_mem_8 (
    .in_4(out_14), .out_6(in_4), .in_1(in_2[3:0]), .in_2(and_1_out), .in_3(decoder_2_out8), .in_5(in_5));
  _4_bit_Mem u_4_bit_mem_9 (
    .in_4(out_14), .out_6(in_4), .in_1(in_2[3:0]), .in_2(and_1_out), .in_3(decoder_2_out9), .in_5(in_5));
  _4_bit_Mem u_4_bit_mem_10 (
    .in_4(out_14), .out_6(in_4), .in_1(in_2[3:0]), .in_2(and_1_out), .in_3(decoder_2_out10), .in_5(in_5));
  _4_bit_Mem u_4_bit_mem_11 (
    .in_4(out_14), .out_6(in_4), .in_1(in_2[3:0]), .in_2(and_1_out), .in_3(decoder_2_out11), .in_5(in_5));
  _4_bit_Mem u_4_bit_mem_12 (
    .in_4(out_14), .out_6(in_4), .in_1(in_2[3:0]), .in_2(and_1_out), .in_3(decoder_2_out12), .in_5(in_5));
  _4_bit_Mem u_4_bit_mem_13 (
    .in_4(out_14), .out_6(in_4), .in_1(in_2[3:0]), .in_2(and_1_out), .in_3(decoder_2_out13), .in_5(in_5));
  _4_bit_Mem u_4_bit_mem_14 (
    .in_4(out_14), .out_6(in_4), .in_1(in_2[3:0]), .in_2(and_1_out), .in_3(decoder_2_out14), .in_5(in_5));
  _4_bit_Mem u_4_bit_mem_15 (
    .in_4(out_14), .out_6(in_4), .in_1(in_2[3:0]), .in_2(and_1_out), .in_3(decoder_2_out15), .in_5(in_5));
  and and_1 (and_1_out, in_1, in_3);
  Pull_Resistor pull_resistor_1 (.node(out_14));
  assign out_14 = OutPuts[7] ? out_15 : 8'bz;  // Controlled_Buffer controlled_buffer_9
  Register register_1 (.D(in_4), .Q(out_15), .clk(and_3_out), .clr(in_5));  // open: en
  and and_2 (and_2_out, and_1_out, OutPuts[6]);
  and and_3 (and_3_out, and_1_out, OutPuts[7]);
  assign out_14 = OutPuts[5] ? out_17 : 8'bz;  // Controlled_Buffer controlled_buffer_10
  assign out_14 = OutPuts[6] ? out_16 : 8'bz;  // Controlled_Buffer controlled_buffer_11
  Register register_2 (.D(in_4), .Q(out_16), .clk(and_2_out), .clr(in_5));  // open: en
  Register register_3 (.D(in_4), .Q(out_17), .clk(and_4_out), .clr(in_5));  // open: en
  and and_4 (and_4_out, and_1_out, OutPuts[5]);
  assign out_14 = OutPuts[4] ? out_18 : 8'bz;  // Controlled_Buffer controlled_buffer_12
  Register register_4 (.D(in_4), .Q(out_18), .clk(and_6_out), .clr(in_5));  // open: en
  Register register_5 (.D(in_4), .Q(out_19), .clk(and_5_out), .clr(in_5));  // open: en
  and and_5 (and_5_out, and_1_out, OutPuts[3]);
  and and_6 (and_6_out, and_1_out, OutPuts[4]);
  assign out_14 = OutPuts[2] ? out_20 : 8'bz;  // Controlled_Buffer controlled_buffer_13
  assign out_14 = OutPuts[3] ? out_19 : 8'bz;  // Controlled_Buffer controlled_buffer_14
  Register register_6 (.D(in_4), .Q(out_20), .clk(and_8_out), .clr(in_5));  // open: en
  and and_7 (and_7_out, and_1_out, OutPuts[1]);
  and and_8 (and_8_out, and_1_out, OutPuts[2]);
  assign out_14 = OutPuts[1] ? out_21 : 8'bz;  // Controlled_Buffer controlled_buffer_15
  Register register_7 (.D(in_4), .Q(out_21), .clk(and_7_out), .clr(in_5));  // open: en
  Register register_8 (.D(in_4), .Q(out_22), .clk(and_9_out), .clr(in_5));  // open: en
  and and_9 (and_9_out, and_1_out, OutPuts[0]);
  assign out_14 = OutPuts[0] ? out_22 : 8'bz;  // Controlled_Buffer controlled_buffer_16
endmodule

module _4_bit_Mem (
  input  [3:0] in_1,
  input  in_2,
  input  in_3,
  input  [7:0] in_4,
  input  in_5,
  output [7:0] out_6
);

  wire [7:0] controlled_buffer_1_out, ram_1_data;

  assign controlled_buffer_1_out = in_3 ? in_4 : 8'bz;  // Controlled_Buffer controlled_buffer_1
  RAM #(.addrWidth(4), .bus("separate")) ram_1 (
    .addr(in_1), .din(controlled_buffer_1_out), .data(ram_1_data), .clk(in_2), .ld(in_2), .clr(in_5));  // open: str, sel
  assign out_6 = in_3 ? ram_1_data : 8'bz;  // Controlled_Buffer controlled_buffer_2
endmodule

module V_Ctrl (
  input  [7:0] in_1,
  input  [7:0] in_2,
  input  [2:0] in_3,
  input  in_4,
  output [7:0] out_5,
  output [7:0] out_6
);

  wire demultiplexer_1_out0, demultiplexer_1_out1, demultiplexer_2_out0, demultiplexer_2_out1, not_1_out,
       or_1_out, or_2_out, t_ff_1_q;
  wire [7:0] controlled_buffer_1_out, controlled_buffer_2_out, register_1_q, register_2_q;

  Demultiplexer #(.enable("false")) demultiplexer_1 (
    .out0(demultiplexer_1_out0), .out1(demultiplexer_1_out1), .in(in_3[1]), .sel(t_ff_1_q));
  Demultiplexer #(.enable("false")) demultiplexer_2 (
    .out0(demultiplexer_2_out0), .out1(demultiplexer_2_out1), .in(in_3[2]), .sel(t_ff_1_q));
  assign controlled_buffer_1_out = t_ff_1_q ? in_1 : 8'bz;  // Controlled_Buffer controlled_buffer_1
  assign controlled_buffer_2_out = not_1_out ? in_1 : 8'bz;  // Controlled_Buffer controlled_buffer_2
  assign controlled_buffer_1_out = not_1_out ? in_2 : 8'bz;  // Controlled_Buffer controlled_buffer_3
  assign controlled_buffer_2_out = t_ff_1_q ? in_2 : 8'bz;  // Controlled_Buffer controlled_buffer_4
  or or_1 (or_1_out, demultiplexer_1_out0, demultiplexer_2_out1);
  or or_2 (or_2_out, demultiplexer_1_out1, demultiplexer_2_out0);
  Register register_1 (.D(controlled_buffer_1_out), .Q(register_1_q), .clk(or_1_out), .clr(in_4));  // open: en
  Register register_2 (.D(controlled_buffer_2_out), .Q(register_2_q), .clk(or_2_out), .clr(in_4));  // open: en
  assign out_6 = not_1_out ? register_1_q : 8'bz;  // Controlled_Buffer controlled_buffer_5
  assign out_5 = t_ff_1_q ? register_1_q : 8'bz;  // Controlled_Buffer controlled_buffer_6
  assign out_6 = t_ff_1_q ? register_2_q : 8'bz;  // Controlled_Buffer controlled_buffer_7
  assign out_5 = not_1_out ? register_2_q : 8'bz;  // Controlled_Buffer controlled_buffer_8
  not not_1 (not_1_out, t_ff_1_q);
  T_Flip_Flop t_ff_1 (.clk(in_3[0]), .T(1'b1), .Q(t_ff_1_q), .reset(in_4));  // open: Qn, preset, en
endmodule
