// Logisim project von harvard cpu 1.circ as structural Verilog: 2 circuits, main circuit main
module main (
);

  wire alu_1_out_5, alu_1_out_6, and_1_out, button_1_out, button_2_out, clock_1_out, or_1_out;
  wire [7:0] acc_q, adder_1_out, alu_1_out_7, multiplexer_1_out, PC_q, ram_1_data, rom_1_data;
  wire [11:8] rom_1_data_2;

  Adder adder_1 (.a(8'h1), .b(PC_q), .out(adder_1_out));  // open: cin, cout
  Clock clock_1 (.out(clock_1_out));
  Button button_1 (.out(button_1_out));
  Button button_2 (.out(button_2_out));
  Multiplexer #(.width(8), .enable("false")) multiplexer_1 (
    .in0(adder_1_out), .in1(rom_1_data), .out(multiplexer_1_out), .sel(alu_1_out_6));
  or or_1 (or_1_out, button_1_out, button_2_out);
  Register #(.trigger("falling")) PC (.D(multiplexer_1_out), .Q(PC_q), .clk(clock_1_out), .clr(or_1_out));  // open: en
  Register acc (.D(alu_1_out_7), .Q(acc_q), .clk(and_1_out), .clr(or_1_out));  // open: en
  and and_1 (and_1_out, clock_1_out, ~alu_1_out_5);  // AND_Gate
  ALU alu_1 (
    .in_2(acc_q), .in_3(ram_1_data), .in_4(rom_1_data), .in_1(rom_1_data_2), .out_5(alu_1_out_5),
    .out_6(alu_1_out_6), .out_7(alu_1_out_7));
  ROM #(.dataWidth(12)) rom_1 (.addr(PC_q), .data({rom_1_data_2, rom_1_data}));  // open: sel
  RAM #(.bus("separate")) ram_1 (
    .addr(rom_1_data), .din(alu_1_out_7), .data(ram_1_data), .str(alu_1_out_5), .clk(alu_1_out_5),
    .clr(button_2_out));  // open: sel, ld

  // Notes on the sheet:
  //   contents of rom_1 (hex, n*v repeats v):
  //   b01 104 a00 203 204 103 9 a09 3 202 204 102 f a00 3 201 204 101 15 a00 3 200 204 100 a03 3
endmodule

module ALU (
  input  [3:0] in_1,
  input  [7:0] in_2,
  input  [7:0] in_3,
  input  [7:0] in_4,
  output out_5,
  output out_6,
  output [7:0] out_7
);

  wire comparator_2_eq, comparator_3_eq;
  wire [7:0] adder_1_out, and_1_out, divider_1_out, multiplier_1_out, not_1_out, or_1_out, subtractor_1_out,
       xor_1_out;

  Adder adder_1 (.a(in_2), .b(in_3), .out(adder_1_out));  // open: cin, cout
  Subtractor subtractor_1 (.a(in_2), .b(in_3), .out(subtractor_1_out));  // open: bin, bout
  Multiplier multiplier_1 (.a(in_2), .b(in_3), .out(multiplier_1_out));  // open: cin, cout
  Divider divider_1 (.a(in_2), .b(in_3), .out(divider_1_out));  // open: upper, rem
  assign and_1_out = in_2 & in_3;  // AND_Gate and_1, 8 bits wide
  assign or_1_out = in_2 | in_3;  // OR_Gate or_1, 8 bits wide
  assign not_1_out = ~in_2;  // NOT_Gate not_1, 8 bits wide
  assign xor_1_out = in_2 ^ in_3;  // XOR_Gate xor_1, 8 bits wide
  Multiplexer #(.select(4), .width(8), .enable("false")) multiplexer_1 (
    .in0(in_2), .in1(in_2), .in2(adder_1_out), .in3(subtractor_1_out), .in4(multiplier_1_out),
    .in5(divider_1_out), .in6(and_1_out), .in7(or_1_out), .in8(xor_1_out), .in9(not_1_out), .in10({8{1'b0}}),
    .in11(in_4), .in15(in_2), .out(out_7), .sel(in_1));  // open: in12, in13, in14
  Comparator #(.width(4), .mode("unsigned")) comparator_1 (.a(4'b0001), .b(in_1), .eq(out_5));  // open: gt, lt
  Comparator #(.width(4), .mode("unsigned")) comparator_2 (
    .a(in_1), .b(4'b0000), .eq(comparator_2_eq));  // open: gt, lt
  Comparator #(.mode("unsigned")) comparator_3 (.a({8{1'b0}}), .b(out_7), .eq(comparator_3_eq));  // open: gt, lt
  and and_2 (out_6, comparator_2_eq, comparator_3_eq);
endmodule
