// Logisim project von neumann cpu 1.circ as structural Verilog: 3 circuits, main circuit main
module main (
);

  wire alu_1_out_4, alu_1_out_5, and_1_out, and_2_out, button_1_out, button_2_out, clock_1_out, nand_1_out,
       or_1_out, or_2_out;
  wire [3:0] instruction_q_2;
  wire [15:0] adder_1_out, adder_2_out, alu_1_out_6, instruction_q, multiplexer_1_out, multiplexer_2_out,
       multiplexer_3_out, program_counter_q, ram_1_data, register_file_1_out_6, register_file_1_out_7;

  Adder #(.width(16)) adder_1 (.a(16'h1), .b(program_counter_q), .out(adder_1_out));  // open: cin, cout
  Clock #(.highDuration(7)) clock_1 (.out(clock_1_out));
  Adder #(.width(16)) adder_2 (.a(16'h1), .b(program_counter_q), .out(adder_2_out));  // open: cin, cout
  Multiplexer #(.width(16), .enable("false")) multiplexer_1 (
    .in0(adder_1_out), .in1(register_file_1_out_7), .out(multiplexer_1_out), .sel(alu_1_out_5));
  Register #(.width(16), .trigger("falling")) program_counter (
    .D(multiplexer_1_out), .Q(program_counter_q), .clk(clock_1_out), .clr(or_1_out));  // open: en
  Button button_1 (.out(button_1_out));
  Button button_2 (.out(button_2_out));
  Multiplexer #(.width(16), .enable("false")) multiplexer_2 (
    .in0(program_counter_q), .in1(adder_2_out), .out(multiplexer_2_out), .sel(alu_1_out_4));
  or or_1 (or_1_out, button_1_out, button_2_out);
  and and_1 (and_1_out, alu_1_out_4, ~instruction_q[0]);  // AND_Gate
  RAM #(.addrWidth(16), .dataWidth(16), .bus("separate")) ram_1 (
    .addr(multiplexer_2_out), .din(register_file_1_out_7), .data(ram_1_data), .str(and_1_out),
    .clk(clock_1_out), .clr(button_2_out));  // open: sel, ld
  Multiplexer #(.width(16), .enable("false")) multiplexer_3 (
    .in0(alu_1_out_6), .in1(ram_1_data), .out(multiplexer_3_out), .sel(alu_1_out_4));
  and and_2 (and_2_out, instruction_q[0], alu_1_out_4);
  Register_File register_file_1 (
    .in_1(multiplexer_3_out), .in_5(or_2_out), .in_4(or_1_out), .in_2(instruction_q_2),
    .in_3(instruction_q[7:4]), .out_6(register_file_1_out_6), .out_7(register_file_1_out_7));
  or or_2 (or_2_out, and_2_out, nand_1_out);
  nand nand_1 (nand_1_out, alu_1_out_4, alu_1_out_5, instruction_q[0]);
  Register #(.width(16)) instruction (
    .D(ram_1_data), .Q({instruction_q[15:12], instruction_q_2, instruction_q[7:0]}), .clk(clock_1_out),
    .clr(or_1_out));  // open: en
  // Probe on {instruction_q[15:12], instruction_q_2, instruction_q[7:0]}
  ALU alu_1 (
    .in_2(register_file_1_out_6), .in_3(register_file_1_out_7), .in_1(instruction_q[15:12]),
    .out_4(alu_1_out_4), .out_5(alu_1_out_5), .out_6(alu_1_out_6));
endmodule

module ALU (
  input  [3:0] in_1,
  input  [15:0] in_2,
  input  [15:0] in_3,
  output out_4,
  output out_5,
  output [15:0] out_6
);

  wire comparator_2_eq, comparator_3_eq;
  wire [15:0] adder_1_out, and_1_out, divider_1_out, multiplier_1_out, not_1_out, or_1_out, subtractor_1_out,
       xor_1_out;

  Adder #(.width(16)) adder_1 (.a(in_2), .b(in_3), .out(adder_1_out));  // open: cin, cout
  Subtractor #(.width(16)) subtractor_1 (.a(in_2), .b(in_3), .out(subtractor_1_out));  // open: bin, bout
  Multiplier #(.width(16)) multiplier_1 (.a(in_2), .b(in_3), .out(multiplier_1_out));  // open: cin, cout
  Divider #(.width(16)) divider_1 (.a(in_2), .b(in_3), .out(divider_1_out));  // open: upper, rem
  assign and_1_out = in_2 & in_3;  // AND_Gate and_1, 16 bits wide
  assign or_1_out = in_2 | in_3;  // OR_Gate or_1, 16 bits wide
  assign not_1_out = ~in_2;  // NOT_Gate not_1, 16 bits wide
  assign xor_1_out = in_2 ^ in_3;  // XOR_Gate xor_1, 16 bits wide
  Multiplexer #(.select(4), .width(16), .enable("false")) multiplexer_1 (
    .in0(in_2), .in1(in_2), .in2(adder_1_out), .in3(subtractor_1_out), .in4(multiplier_1_out),
    .in5(divider_1_out), .in6(and_1_out), .in7(or_1_out), .in8(xor_1_out), .in9(not_1_out),
    .in10({16{1'b0}}), .in15(in_2), .out(out_6), .sel(in_1));  // open: in11, in12, in13, in14
  Comparator #(.width(4), .mode("unsigned")) comparator_1 (.a(4'b0001), .b(in_1), .eq(out_4));  // open: gt, lt
  Comparator #(.width(4), .mode("unsigned")) comparator_2 (
    .a(in_1), .b(4'b0000), .eq(comparator_2_eq));  // open: gt, lt
  Comparator #(.width(16), .mode("unsigned")) comparator_3 (
    .a({16{1'b0}}), .b(out_6), .eq(comparator_3_eq));  // open: gt, lt
  and and_2 (out_5, comparator_2_eq, comparator_3_eq);
endmodule

module Register_File (
  input  [15:0] in_1,
  input  [3:0] in_2,
  input  [3:0] in_3,
  input  in_4,
  input  in_5,
  output [15:0] out_6,
  output [15:0] out_7
);

  wire and_1_out, clock_1_out, decoder_1_out0, decoder_1_out1, decoder_1_out2, decoder_1_out3,
       decoder_1_out4, decoder_1_out5, decoder_1_out6, decoder_1_out7, decoder_1_out8, decoder_1_out9,
       decoder_1_out10, decoder_1_out11, decoder_1_out12, decoder_1_out13, decoder_1_out14, decoder_1_out15;
  wire [15:0] register_1_q, register_2_q, register_3_q, register_4_q, register_5_q, register_6_q,
       register_7_q, register_8_q, register_9_q, register_10_q, register_11_q, register_12_q, register_13_q,
       register_14_q, register_15_q;

  Decoder #(.select(4), .enable("false")) decoder_1 (
    .out0(decoder_1_out0), .out1(decoder_1_out1), .out2(decoder_1_out2), .out3(decoder_1_out3),
    .out4(decoder_1_out4), .out5(decoder_1_out5), .out6(decoder_1_out6), .out7(decoder_1_out7),
    .out8(decoder_1_out8), .out9(decoder_1_out9), .out10(decoder_1_out10), .out11(decoder_1_out11),
    .out12(decoder_1_out12), .out13(decoder_1_out13), .out14(decoder_1_out14), .out15(decoder_1_out15),
    .sel(in_2));
  and and_1 (and_1_out, clock_1_out, in_5);
  Clock clock_1 (.out(clock_1_out));
  Register #(.width(16), .trigger("falling")) register_1 (
    .D(in_1), .en(decoder_1_out1), .Q(register_1_q), .clk(and_1_out), .clr(in_4));
  Register #(.width(16)) register_2 (.D(in_1), .en(decoder_1_out2), .Q(register_2_q), .clk(and_1_out), .clr(in_4));
  Register #(.width(16)) register_3 (.D(in_1), .en(decoder_1_out3), .Q(register_3_q), .clk(and_1_out), .clr(in_4));
  Register #(.width(16)) register_4 (.D(in_1), .en(decoder_1_out4), .Q(register_4_q), .clk(and_1_out), .clr(in_4));
  Register #(.width(16)) register_5 (.D(in_1), .en(decoder_1_out5), .Q(register_5_q), .clk(and_1_out), .clr(in_4));
  Register #(.width(16)) register_6 (.D(in_1), .en(decoder_1_out6), .Q(register_6_q), .clk(and_1_out), .clr(in_4));
  Register #(.width(16)) register_7 (.D(in_1), .en(decoder_1_out7), .Q(register_7_q), .clk(and_1_out), .clr(in_4));
  Register #(.width(16)) register_8 (.D(in_1), .en(decoder_1_out8), .Q(register_8_q), .clk(and_1_out), .clr(in_4));
  Register #(.width(16)) register_9 (.D(in_1), .en(decoder_1_out9), .Q(register_9_q), .clk(and_1_out), .clr(in_4));
  Register #(.width(16)) register_10 (.D(in_1), .en(decoder_1_out10), .Q(register_10_q), .clk(and_1_out), .clr(in_4));
  Register #(.width(16)) register_11 (.D(in_1), .en(decoder_1_out11), .Q(register_11_q), .clk(and_1_out), .clr(in_4));
  Register #(.width(16)) register_12 (.D(in_1), .en(decoder_1_out12), .Q(register_12_q), .clk(and_1_out), .clr(in_4));
  Register #(.width(16)) register_13 (.D(in_1), .en(decoder_1_out13), .Q(register_13_q), .clk(and_1_out), .clr(in_4));
  Register #(.width(16)) register_14 (.D(in_1), .en(decoder_1_out14), .Q(register_14_q), .clk(and_1_out), .clr(in_4));
  Register #(.width(16)) register_15 (.D(in_1), .en(decoder_1_out15), .Q(register_15_q), .clk(and_1_out), .clr(in_4));
  Multiplexer #(.select(4), .width(16), .enable("false")) multiplexer_1 (
    .in0({16{1'b0}}), .in1(register_1_q), .in2(register_2_q), .in3(register_3_q), .in4(register_4_q),
    .in5(register_5_q), .in6(register_6_q), .in7(register_7_q), .in8(register_8_q), .in9(register_9_q),
    .in10(register_10_q), .in11(register_11_q), .in12(register_12_q), .in13(register_13_q),
    .in14(register_14_q), .in15(register_15_q), .out(out_6), .sel(in_3));
  Multiplexer #(.select(4), .width(16), .enable("false")) multiplexer_2 (
    .in0({16{1'b0}}), .in1(register_1_q), .in2(register_2_q), .in3(register_3_q), .in4(register_4_q),
    .in5(register_5_q), .in6(register_6_q), .in7(register_7_q), .in8(register_8_q), .in9(register_9_q),
    .in10(register_10_q), .in11(register_11_q), .in12(register_12_q), .in13(register_13_q),
    .in14(register_14_q), .in15(register_15_q), .out(out_7), .sel(in_2));
  Pull_Resistor pull_resistor_1 (.node(in_2));
  Pull_Resistor pull_resistor_2 (.node(in_3));
endmodule
